// Logisim project Adder__Final.circ as structural Verilog: 1 circuit, main circuit main
module main (
  input  in_1,
  input  in_2,
  input  in_3,
  input  in_4,
  input  in_5,
  input  in_6,
  input  in_7,
  input  in_8,
  input  in_9,
  input  in_10,
  input  in_11,
  input  in_12
);

  wire n7408_1_pin3, n7408_1_pin6, n7408_1_pin8, n7408_1_pin11, n7408_3_pin3, n7408_3_pin6, n7408_3_pin8,
       n7408_3_pin11, n7408_5_pin3, n7408_5_pin6, n7408_5_pin8, n7408_5_pin11, n7432_1_pin6, n7432_1_pin11,
       n7432_1_pin12, n7432_1_pin13, n7432_2_pin6, n7432_2_pin8, n7432_2_pin9, n7432_2_pin10, n7432_2_pin11,
       n7432_2_pin12, n7432_2_pin13, n7432_3_pin6, n7432_3_pin12, n7432_3_pin13, n7486_1_pin1, n7486_1_pin3,
       n7486_1_pin6, n7486_1_pin8, n7486_1_pin11, n7486_1_pin13, n7486_2_pin1, n7486_2_pin3, n7486_2_pin5,
       n7486_2_pin6, n7486_2_pin8, n7486_2_pin9, n7486_2_pin11, n7486_2_pin13, n7486_3_pin3, n7486_3_pin6,
       n7486_4_pin1, n7486_4_pin3, n7486_4_pin11, n7486_4_pin13, n7486_5_pin3, n7486_5_pin5, n7486_5_pin6,
       n7486_5_pin8, n7486_5_pin9, n7486_5_pin11, n7486_6_pin3;

  _7486 u_7486_1 (
    .pin1(n7486_1_pin1), .pin2(in_3), .pin3(n7486_1_pin3), .pin4(n7486_1_pin3), .pin5(in_4),
    .pin6(n7486_1_pin6), .pin13(n7486_1_pin13), .pin12(in_5), .pin11(n7486_1_pin11), .pin10(n7486_1_pin11),
    .pin9(in_6), .pin8(n7486_1_pin8));
  _7408 u_7408_1 (
    .pin1(in_3), .pin2(n7486_1_pin1), .pin3(n7408_1_pin3), .pin4(n7486_1_pin3), .pin5(in_4),
    .pin6(n7408_1_pin6), .pin13(n7486_1_pin13), .pin12(in_5), .pin11(n7408_1_pin11), .pin10(n7486_1_pin11),
    .pin9(in_6), .pin8(n7408_1_pin8));
  _7432 u_7432_1 (
    .pin1(n7408_1_pin3), .pin2(n7408_1_pin6), .pin3(n7486_1_pin13), .pin4(n7408_1_pin11),
    .pin5(n7408_1_pin8), .pin6(n7432_1_pin6), .pin13(n7432_1_pin13), .pin12(n7432_1_pin12),
    .pin11(n7432_1_pin11));  // open: pin10, pin9, pin8
  _7486 u_7486_2 (
    .pin1(n7486_2_pin1), .pin2(n7486_1_pin6), .pin3(n7486_2_pin3), .pin4(n7486_2_pin3), .pin5(n7486_2_pin5),
    .pin6(n7486_2_pin6), .pin13(n7486_2_pin13), .pin12(n7486_1_pin8), .pin11(n7486_2_pin11),
    .pin10(n7486_2_pin11), .pin9(n7486_2_pin9), .pin8(n7486_2_pin8));
  _7486 u_7486_3 (
    .pin1(n7432_1_pin6), .pin2(in_1), .pin3(n7486_3_pin3), .pin4(n7486_3_pin3), .pin5(in_2),
    .pin6(n7486_3_pin6));  // open: pin13, pin12, pin11, pin10, pin9, pin8
  _7408 u_7408_2 (
    .pin1(n7432_1_pin6), .pin2(in_1), .pin3(n7432_1_pin12), .pin4(n7486_3_pin3), .pin5(in_2),
    .pin6(n7432_1_pin13));  // open: pin13, pin12, pin11, pin10, pin9, pin8
  _7408 u_7408_3 (
    .pin1(n7486_1_pin6), .pin2(n7486_2_pin1), .pin3(n7408_3_pin3), .pin4(n7486_2_pin3), .pin5(n7486_2_pin5),
    .pin6(n7408_3_pin6), .pin13(n7486_2_pin13), .pin12(n7486_1_pin8), .pin11(n7408_3_pin11),
    .pin10(n7486_2_pin11), .pin9(n7486_2_pin9), .pin8(n7408_3_pin8));
  _7432 u_7432_2 (
    .pin1(n7408_3_pin3), .pin2(n7408_3_pin6), .pin3(n7486_2_pin13), .pin4(n7408_3_pin11),
    .pin5(n7408_3_pin8), .pin6(n7432_2_pin6), .pin13(n7432_2_pin13), .pin12(n7432_2_pin12),
    .pin11(n7432_2_pin11), .pin10(n7432_2_pin10), .pin9(n7432_2_pin9), .pin8(n7432_2_pin8));
  _7486 u_7486_4 (
    .pin1(n7486_4_pin1), .pin2(in_9), .pin3(n7486_4_pin3), .pin4(n7486_4_pin3), .pin5(in_10),
    .pin6(n7486_2_pin5), .pin13(n7486_4_pin13), .pin12(in_11), .pin11(n7486_4_pin11), .pin10(n7486_4_pin11),
    .pin9(in_12), .pin8(n7486_2_pin9));
  _7486 u_7486_5 (
    .pin1(n7432_2_pin6), .pin2(n7486_3_pin6), .pin3(n7486_5_pin3), .pin4(n7486_5_pin3), .pin5(n7486_5_pin5),
    .pin6(n7486_5_pin6), .pin13(n7432_2_pin11), .pin12(n7432_1_pin11), .pin11(n7486_5_pin11),
    .pin10(n7486_5_pin11), .pin9(n7486_5_pin9), .pin8(n7486_5_pin8));
  // RGBLED rgbled_1: pin names not known; wires that end beside it: n7432_2_pin8
  // RGBLED rgbled_2: pin names not known; wires that end beside it: n7486_5_pin8
  _7408 u_7408_4 (
    .pin1(n7432_2_pin6), .pin2(n7486_3_pin6), .pin3(n7432_2_pin12), .pin4(n7486_5_pin3), .pin5(n7486_5_pin5),
    .pin6(n7432_2_pin13), .pin13(n7432_2_pin11), .pin12(n7432_1_pin11), .pin11(n7432_2_pin10),
    .pin10(n7486_5_pin11), .pin9(n7486_5_pin9), .pin8(n7432_2_pin9));
  _7408 u_7408_5 (
    .pin1(in_9), .pin2(n7486_4_pin1), .pin3(n7408_5_pin3), .pin4(n7486_4_pin3), .pin5(in_10),
    .pin6(n7408_5_pin6), .pin13(n7486_4_pin13), .pin12(in_11), .pin11(n7408_5_pin11), .pin10(n7486_4_pin11),
    .pin9(in_12), .pin8(n7408_5_pin8));
  // RGBLED rgbled_3: pin names not known; wires that end beside it: n7486_5_pin6
  // RGBLED rgbled_4: pin names not known; wires that end beside it: n7486_2_pin8
  // RGBLED rgbled_5: pin names not known; wires that end beside it: n7486_2_pin6
  _7432 u_7432_3 (
    .pin1(n7408_5_pin3), .pin2(n7408_5_pin6), .pin3(n7486_4_pin13), .pin4(n7408_5_pin11),
    .pin5(n7408_5_pin8), .pin6(n7432_3_pin6), .pin13(n7432_3_pin13), .pin12(n7432_3_pin12),
    .pin11(n7486_5_pin9));  // open: pin10, pin9, pin8
  _7486 u_7486_6 (
    .pin1(n7432_3_pin6), .pin2(in_7), .pin3(n7486_6_pin3), .pin4(n7486_6_pin3), .pin5(in_8),
    .pin6(n7486_5_pin5));  // open: pin13, pin12, pin11, pin10, pin9, pin8
  _7408 u_7408_6 (
    .pin1(n7432_3_pin6), .pin2(in_7), .pin3(n7432_3_pin12), .pin4(n7486_6_pin3), .pin5(in_8),
    .pin6(n7432_3_pin13));  // open: pin13, pin12, pin11, pin10, pin9, pin8
  // also tied to GND on the sheet: {n7486_1_pin1, n7486_2_pin1, n7486_4_pin1}
endmodule
